# Fritzing sketch button (saved by Fritzing 0.6.3b)
breadboards: 1

parts:
  Arduino1 = Arduino
  LED1 = LED - 5mm [color="Red (633nm)" package="5 mm [THT]"]
  R1 = Resistor [tolerance=±5% resistance=10 package=THT]  # not connected
  S1 = Pushbutton [package="[THT]"]

nets:
  N1: Arduino1.GND, LED1.cathode, S1.Pin_1, S1.Pin_2
  N2: Arduino1.D13, LED1.anode
